# Fritzing sketch schematics_protoboard (saved by Fritzing 0.9.3b)
circuit board: 8.46667cm x 5.64444cm
breadboards: 1
stripboards: 2

parts:
  Part1 = Arduino Uno (Rev3)
  R1 = Resistor [tolerance=±5% resistance=1k package="2010 [SMD]"]
  R4 = Resistor [tolerance=±5% resistance=1k package="2010 [SMD]"]
  S1 = SWITCH-MOMENTARY-2 [package=tactile-pth-12mm]
  S2 = SWITCH-MOMENTARY-2 [package=tactile-pth-12mm]
  S3 = SWITCH-MOMENTARY-2 [package=tactile-pth-12mm]
  S4 = SWITCH-MOMENTARY-2 [package=tactile-pth-12mm]
  S5 = SWITCH-MOMENTARY-2 [package=tactile-pth-12mm]
  R5 = Resistor [tolerance=±5% resistance=10k package="2010 [SMD]"]
  R6 = Resistor [tolerance=±5% resistance=10k package="2010 [SMD]"]
  R7 = Resistor [tolerance=±5% resistance=10k package="2010 [SMD]"]  # not connected
  R8 = Resistor [tolerance=±5% resistance=10k package="2010 [SMD]"]
  R9 = Resistor [tolerance=±5% resistance=10k package="2010 [SMD]"]

nets (from the breadboard view):
  N1: Part1.D8, Part1.D9_PWM, Part1.D10_PWM/SS, Part1.D11_PWM/MOSI, Part1.D12/MISO, Part1.GND, S1.2, S2.2, S3.2, S4.2, S5.2, R5.Pin_0, R5.Pin_1, R6.Pin_0, R6.Pin_1, R8.Pin_0, R8.Pin_1, R9.Pin_0, R9.Pin_1
  N2: Part1.D3_PWM, R4.Pin_0
  N3: Part1.D4, R1.Pin_0
  N4: Part1.5V, R1.Pin_1, R4.Pin_1, S1.1, S2.1, S3.1, S4.1, S5.1

notes:
  FROM GuitarHero Wire:
  data:
  vcc: 4.5v
  GND
  CLK
  COMMAND (W), Attention (Y)
  from first row of 5 btns
